# Fritzing sketch motherboard (saved by Fritzing 0.9.3b)
stripboards: 1

parts:
  IC1 = 6n137 Optocoupler [package="DIP (Dual Inline) [THT]"]
  R1 = Resistor [tolerance=±5% resistance=220 package=THT]
  R2 = Resistor [tolerance=±5% resistance=220 package=THT]
  R3 = Resistor [tolerance=±5% resistance=10k package=THT]
  IC2 = Hex Inverter Schmitt Trigger SN74HC14 [package="DIP (Dual Inline)"]
  IC3 = SPEAKJET [package=dil18]
  R4 = Resistor [tolerance=±5% resistance=1k package=THT]
  R5 = Resistor [tolerance=±5% resistance=27k package=THT]
  C1 = Ceramic Capacitor [capacitance=10nF package="100 mil [THT, multilayer]"]
  C2 = Ceramic Capacitor [capacitance=10nF package="100 mil [THT, multilayer]"]
  C3 = Electrolytic Capacitor [capacitance=10µF package="100 mil [THT, electrolytic]"]
  X1 = SparkFun - microSD Transflash
  IC4 = TTS256 [package="DIP (Dual Inline) [THT]"]
  D1 = Small signal Diode flat 300mil [part_number=1N4148 package="300 mil [THT]"]
  R7 = Resistor [tolerance=±5% resistance=220 package=THT]
  R8 = Resistor [tolerance=±5% resistance=220 package=THT]
  C4 = Electrolytic Capacitor [capacitance=10µF package="100 mil [THT, electrolytic]"]
  R6 = Resistor [tolerance=±5% resistance=27k package=THT]

nets:
  N1: IC1.Vf+, R1.Pin_1, D1.cathode
  N2: IC1.Vf-, R2.Pin_1, D1.anode
  GND/MIDI_IN_GND/MIDI_THRU_GND: IC1.GND, IC2.GND, IC3.E7_RC1, IC3.E6_RC0, IC3.E5, IC3.E4, IC3.GND, IC3.E3, IC3.E2, IC3.E1, IC3.E0, IC3.M0, C1.0, C2.0, X1.GND, IC4.pin14, C4.-
  MIDI_RX: IC1.Vo, R3.Pin_0, IC2.6A
  5V: IC1.Vcc, R3.Pin_1, IC2.VCC, IC3.VCC, R4.Pin_1, IC4.pin28, R8.Pin_0, C4.+
  MIDI_IN_4: R1.Pin_0
  MIDI_IN_5: R2.Pin_0
  N3: IC2.5Y, R7.Pin_0
  N4: IC2.5A, IC2.6Y
  SPKJ_TX: IC3.RX
  SPKJ_RST: IC3.RST
  N5: IC3.M1, R4.Pin_0
  SPKJ_BHF: IC3.D2_BHF
  SPKJ_SPK: IC3.D1_SPK
  SPKJ_RDY: IC3.D0_RDY
  N6: IC3.VOICE, R5.Pin_0
  N7: R5.Pin_1, C1.1, R6.Pin_0
  N8: C2.1, C3.+, R6.Pin_1
  3.3V: X1.VCC
  µSD_CS: X1.CS
  µSD_MOSI: X1.MOSI
  µSD_CLK: X1.SCK
  µSD_MISO: X1.MISO
  TTS256_RST: IC4.pin1
  TTS256_TX: IC4.pin18
  TTS256_WAIT: IC4.pin20
  TTS256_RX: IC4.pin24
  MIDI_THRU_5: R7.Pin_1
  MIDI_THRU_4: R8.Pin_1

notes:
  Sing'n'Spell, 1.0.0
  MIDI_IN_DIN_5
  MIDI_IN_DIN_4
  MIDI_IN_DIN_GND
  MIDI_THRU_DIN_4
  MIDI_THRU_DIN_5
  MIDI_IN_UART

custom parts:
  6n137 Optocoupler: 6n137 fast Optocoupler. With 8 pins on a 300mil dual inline package (DIP) footprint. Ve is strobe input. Output is inverting.
  SparkFun - microSD Transflash: https://www.sparkfun.com/products/544 Breakout board for the microSD socket that is not much bigger than your fingernail. Compatible with the SPI interface found on any SD card, this tiny form factor was created for cell phone storage and is perfect for your next MP3 project! Board comes fully assembled and tested. The bare socket is available.
  TTS256: The TTS256 is an 8-bit microprocessor programmed with 600 letter-to-sound rules for the automatic, real-time translation of English text to allophone addresses. Combined with the Magnevation SpeakJet or the Savage Innovations SpeakGin, the TTS256 makes a complete text-to-speech solution.
  Small signal Diode flat 300mil: Small signal diode such as the 1n4148 Footprint: mounted flat on 300mil centers.
